# Fritzing sketch OptoInterrupterHack (saved by Fritzing 0.7.7b)
breadboards: 1

parts:
  S1 = Pushbutton [package="[THT]"]
  Photoresistor = Photocell (LDR) [package=THT]
  Infrared_LED = LED - 3mm [color="Red (633nm)" package="3 mm [THT]"]
  VCC1 = 4 x AAA Battery Mount
  VCC2 = 4 x AAA Battery Mount
  This_LED_will_be_on_when_shwitch_is_on = LED - 3mm [color="Red (633nm)" package="3 mm [THT]"]
  R1 = Resistor [tolerance=±5% resistance=220 package=THT]
  R2 = Resistor [tolerance=±5% resistance=220 package=THT]

nets:
  N1: S1.Pin_1, S1.Pin_2, VCC1.-
  N2: S1.Pin_3, S1.Pin_4, Infrared_LED.cathode
  N3: Photoresistor.pin_0, This_LED_will_be_on_when_shwitch_is_on.anode
  N4: Photoresistor.pin_1, R2.Pin_1
  N5: Infrared_LED.anode, R1.Pin_1
  N6: VCC1.+, R1.Pin_0
  N7: VCC2.-, This_LED_will_be_on_when_shwitch_is_on.cathode
  N8: VCC2.+, R2.Pin_0
